# Fritzing sketch agriduino (saved by Fritzing 0.9.2b)
circuit board: 13.5284cm x 7.31654cm
breadboards: 1

parts:
  Part1 = Arduino Uno (Rev3)
  DHT2 = DHT11 Humitidy and Temperature Sensor
  R1 = PHOTOCELL [package=photocell-kit]
  R3 = Resistor [tolerance=±5% resistance=10k package=THT]
  D1 = Schottky Diode [part_number=1N5817 package="300 mil [THT]"]
  Q1 = NPN-Transistor [package="TO92 [THT]"]
  R4 = Resistor [tolerance=±5% resistance=220 package=THT]
  R2 = Resistor [tolerance=±5% resistance=10k package=THT]
  M1 = DC Motor
  Part2 = FC-28 Soil Hygrometer Module
  Part3 = FC-28 Soil Hygrometer Module - Probe
  C1 = Capacitor Polarized [package=cpol-radial-10uf-25v]

nets:
  N1: Part1.A0, Part2.AO
  N2: Part1.A5/SCL, R1.P$1, R2.Pin_1
  N3: Part1.D12/MISO, DHT2.DATA, R3.Pin_0
  N4: Part1.D7, R4.Pin_1
  N5: Part1.RESET, C1.+
  5V: Part1.5V, DHT2.VDD, R1.P$2, D1.cathode, M1.pin_2, Part2.VCC, C1.-
  GND: Part1.GND, DHT2.GND, R3.Pin_1, Q1.C, R2.Pin_0, Part2.GND
  N6: D1.anode, Q1.E, M1.pin_1
  N7: Q1.B, R4.Pin_0
  N8: Part2.POS, Part3.POS
  N9: Part2.NEG, Part3.NEG

custom parts:
  DHT11 Humitidy and Temperature Sensor: DHT11 Humidity and Temperature Sensor
  FC-28 Soil Hygrometer Module: The FC-28 is a soil hygrometer module that uses the Texas Instruments LM393 comparator chip to provide an analog measurement of soil humidity. The digital output is high when soil moisture is over a certain threshold, as determined by adjusting the potentiometer.
  FC-28 Soil Hygrometer Module - Probe: The FC-28 is a soil hygrometer module that uses the Texas Instruments LM393 comparator chip to provide an analog measurement of soil humidity.
